# Fritzing sketch sketch (saved by Fritzing 0.9.3b)
circuit board: 8.46667cm x 5.64444cm
breadboards: 1

parts:
  S1 = Momentary Switch [package=ksa_sealed_tac_switch]
  S2 = Momentary Switch [package=ksa_sealed_tac_switch]
  S3 = Toggle Switch [package=THT]
  S4 = Toggle Switch [package=THT]
  S5 = Toggle Switch [package=THT]
  S6 = Toggle Switch [package=THT]
  LED1 = smd LED [color="Red (633nm)" package="0603 [SMD]"]
  LED2 = smd LED [color="Yellow (595nm)" package="0603 [SMD]"]
  LED3 = smd LED [color="Green (555nm)" package="0603 [SMD]"]
  U1 = POT [package=pot_mammoth]
  Part2 = Arduino Uno (Rev3) - ICSP
  Grove1 = Grove OLED 128x96
  J1 = Piezo Speaker
  R2 = Resistor [tolerance=±5% resistance=220 package=THT]
  R4 = Resistor [tolerance=±5% resistance=100 package="0805 [SMD]"]
  R5 = Resistor [tolerance=±5% resistance=220 package=THT]
  R6 = Resistor [tolerance=±5% resistance=220 package=THT]
  R7 = Resistor [tolerance=±5% resistance=220 package=THT]
  R8 = Resistor [tolerance=±5% resistance=220 package="0402 [SMD]"]
  R9 = Resistor [tolerance=±5% resistance=1k package=THT]
  R10 = Resistor [tolerance=±5% resistance=1k package=THT]
  R11 = Resistor [tolerance=±5% resistance=1k package=THT]
  R12 = Resistor [tolerance=±5% resistance=1k package=THT]

nets:
  N1: S1.1, R2.Pin_1
  N2: S1.2, Part2.D8
  5V: S1.3, S2.3, S3.COM, S4.COM, S5.COM, S6.COM, U1.E, Part2.5V, Grove1.VCC, J1.pin1
  N3: S2.1, R8.Pin_1
  N4: S2.2, Part2.D2
  N5: S3.L1, Part2.D7, R10.Pin_0
  N6: S4.L1, Part2.D5_PWM, R12.Pin_0
  N7: S5.L1, Part2.D4, R11.Pin_0
  N8: S6.L1, Part2.D6_PWM, R9.Pin_0
  GND: LED1.cathode, LED2.cathode, LED2.anode, LED3.cathode, U1.S, Part2.GND, Grove1.GND, R2.Pin_0, R6.Pin_0, R8.Pin_0
  N9: LED1.anode, R5.Pin_0
  N10: LED3.anode, R7.Pin_0
  N11: U1.A, Part2.A0
  N12: Part2.A4/SDA, Grove1.SDA
  N13: Part2.A5/SCL, Grove1.SCL
  N14: Part2.D9_PWM, R7.Pin_1
  N15: Part2.D10_PWM/SS, R6.Pin_1
  N16: Part2.D11_PWM/MOSI, R5.Pin_1
  N17: Part2.D3_PWM, R4.Pin_0
  N18: J1.pin2, R4.Pin_1
  N19: R9.Pin_1, R10.Pin_1, R11.Pin_1, R12.Pin_1

notes:
  This is actually a Grove-LCD RGB (not an OLED) - wiring is the same
